# Fritzing sketch circutfz (saved by Fritzing 0.6.3b)
breadboards: 1

parts:
  LCD1 = LCD screen
  T1 = LM35 Temperature Sensor [package="TO92 [THT]"]  # not connected
  Arduino1 = Arduino Mega
  R1 = Resistor [tolerance=±5% resistance=4.7k package=THT]
  J1 = screw terminal, 4 pins

nets:
  N1: LCD1.RS, Arduino1.D12
  N2: LCD1.E, Arduino1.D11
  N3: LCD1.DB4, Arduino1.D5
  N4: LCD1.DB5, Arduino1.D4
  N5: LCD1.DB6, Arduino1.D3
  N6: LCD1.DB7, Arduino1.D2
  N7: Arduino1.D10, R1.Pin_1, J1.pin2
  N8: Arduino1.+5V, R1.Pin_0, J1.pin1
  N9: Arduino1.GND, J1.pin4
